# Fritzing sketch three_joysticks (saved by Fritzing 1.0.5)
breadboards: 1

parts:
  U1 = Thumb Joystick [package=joystick]
  S1 = JOYSTICK_MINI [package=joystick_mini]  # not connected
  R1 = TRIMPOT [maximum_resistance=10kΩ knob_status=50% power=0.5W package=3386u]
  R2 = TRIMPOT [maximum_resistance=10kΩ knob_status=50% power=0.5W package=3386u]

nets:
  N1: U1.V+, U1.H+, R1.CW, R2.CW
  N2: U1.SEL-, U1.H-, U1.V-, R1.CCW, R2.CCW
